// Logisim project main.circ as structural Verilog: 1 circuit, main circuit main
module main (
  input  in_1,
  output Frame_Printed
);

  wire clc, clock_1_out, not_1_out, or_1_out, readConsole, RESET_MEMORY_COUNTER_out, uart_1_p1, uart_1_p2,
       uart_1_p8, undriven;
  wire [7:0] ram_1_data;
  wire [11:0] adder_1_out, register_1_q;

  Clock clock_1 (.out(clock_1_out));
  buf or_1 (or_1_out, RESET_MEMORY_COUNTER_out);  // OR_Gate
  Button RESET_MEMORY_COUNTER (.out(RESET_MEMORY_COUNTER_out));
  not not_1 (not_1_out, Frame_Printed);
  // NOT_Gate not_2 has open pins: in=not_1_out, out=open
  Register #(.width(12)) register_1 (.D(adder_1_out), .Q(register_1_q), .clk(clc), .clr(or_1_out));  // open: en
  not not_3 (readConsole, Frame_Printed);
  and and_1 (clc, not_1_out, clock_1_out);
  Comparator #(.width(12)) comparator_1 (.a(register_1_q), .b(12'h16), .eq(Frame_Printed));  // open: gt, lt
  Adder #(.width(12)) adder_1 (.a(register_1_q), .b(12'h1), .out(adder_1_out));  // open: cin, cout
  RAM #(.addrWidth(12)) ram_1 (.addr(register_1_q), .data(ram_1_data), .clk(undriven));  // open: sel, ld, clr
  // Probe on ram_1_data
  // UART uart_1: pin names not known; wires that end beside it: uart_1_p1, uart_1_p2, uart_1_p1, ram_1_data, uart_1_p2, clc, in_1, uart_1_p8, uart_1_p8, readConsole

  // Notes on the sheet:
  //   ВЫСОТА(36)
  //   ШИРИНА(76)
  //   Print Frame
  //   12 бит адрес
  //   2736 СИМВОЛОВ ВСЕГО
endmodule
